// Logisim project Traffic_Light_Project.circ as structural Verilog: 4 circuits, main circuit main
module main (
  input  [5:0] in_1,
  input  Reset,
  input  in_3,
  input  E,
  input  X
);

  wire clock_1_out, state_to_lights_1_le_g, state_to_lights_1_le_r, state_to_lights_1_le_y,
       state_to_lights_1_lx_g, state_to_lights_1_lx_r, state_to_lights_1_lx_y;
  wire [3:0] state_to_count_1_c_0;
  wire [5:0] multiplexer_1_out, register_1_q, state_transition_1_o_0;

  State_Transition state_transition_1 (
    .S_5(register_1_q[5]), .S_4(register_1_q[4]), .S_3(register_1_q[3]), .S_2(register_1_q[2]),
    .S_1(register_1_q[1]), .S_0(register_1_q[0]), .Enter(E), .Exit(X), .O_5(state_transition_1_o_0[5]),
    .O_4(state_transition_1_o_0[4]), .O_3(state_transition_1_o_0[3]), .O_2(state_transition_1_o_0[2]),
    .O_1(state_transition_1_o_0[1]), .O_0(state_transition_1_o_0[0]));
  Register #(.width(6)) register_1 (
    .D(multiplexer_1_out), .en(in_3), .clk(clock_1_out), .Q(register_1_q));  // open: clr
  Multiplexer #(.width(6)) multiplexer_1 (
    .in0(in_1), .in1(state_transition_1_o_0), .out(multiplexer_1_out), .sel(Reset));
  Clock clock_1 (.out(clock_1_out));
  LED led_1 (.in(state_to_lights_1_le_r));
  LED Entrance_Light (.in(state_to_lights_1_le_y));
  LED led_2 (.in(state_to_lights_1_le_g));
  State_to_Lights state_to_lights_1 (
    .S_5(register_1_q[5]), .S_4(register_1_q[4]), .S_3(register_1_q[3]), .S_2(register_1_q[2]),
    .S_1(register_1_q[1]), .S_0(register_1_q[0]), .LE_R(state_to_lights_1_le_r),
    .LE_Y(state_to_lights_1_le_y), .LE_G(state_to_lights_1_le_g), .LX_R(state_to_lights_1_lx_r),
    .LX_Y(state_to_lights_1_lx_y), .LX_G(state_to_lights_1_lx_g));
  LED led_3 (.in(state_to_lights_1_lx_r));
  LED Exit_Light (.in(state_to_lights_1_lx_y));
  LED led_4 (.in(state_to_lights_1_lx_g));
  State_to_Count state_to_count_1 (
    .S_5(register_1_q[5]), .S_4(register_1_q[4]), .S_3(register_1_q[3]), .S_2(register_1_q[2]),
    .S_1(register_1_q[1]), .S_0(register_1_q[0]), .C_3(state_to_count_1_c_0[3]),
    .C_2(state_to_count_1_c_0[2]), .C_1(state_to_count_1_c_0[1]), .C_0(state_to_count_1_c_0[0]));
  Hex_Digit_Display hex_digit_display_1 (.value(state_to_count_1_c_0));  // open: dp
endmodule

module State_to_Count (
  input  S_5,
  input  S_4,
  input  S_3,
  input  S_2,
  input  S_1,
  input  S_0,
  output C_3,
  output C_2,
  output C_1,
  output C_0
);

  wire and_1_out, and_2_out, and_3_out, and_4_out, and_5_out, and_6_out, and_7_out, and_8_out, and_9_out,
       and_10_out, and_11_out, and_12_out, and_13_out, and_14_out, and_15_out, and_16_out, and_17_out,
       and_18_out, and_19_out, and_20_out, and_21_out, not_1_out, not_2_out, not_3_out, not_4_out, not_5_out,
       not_6_out;

  not not_1 (not_1_out, S_5);
  not not_2 (not_2_out, S_4);
  not not_3 (not_3_out, S_3);
  not not_4 (not_4_out, S_2);
  not not_5 (not_5_out, S_1);
  not not_6 (not_6_out, S_0);
  and and_1 (and_1_out, S_5, S_2, S_1, S_0);
  and and_2 (and_2_out, not_2_out, S_3, not_4_out, not_5_out);
  or or_1 (C_3, and_1_out, and_2_out, and_3_out);
  and and_3 (and_3_out, S_5, S_3);
  and and_4 (and_4_out, S_5, not_3_out, not_4_out);
  and and_5 (and_5_out, S_4, S_3);
  and and_6 (and_6_out, not_2_out, not_3_out, S_2, not_5_out);
  and and_7 (and_7_out, not_2_out, not_3_out, S_2, not_6_out);
  and and_8 (and_8_out, not_1_out, not_3_out, S_2, S_1, S_0);
  and and_9 (and_9_out, S_4, not_3_out, not_5_out);
  and and_10 (and_10_out, S_3, S_2, S_1, S_0);
  and and_11 (and_11_out, S_5, not_3_out, not_5_out);
  and and_12 (and_12_out, not_1_out, not_2_out, not_3_out, S_1);
  and and_13 (and_13_out, not_3_out, not_4_out, S_1);
  and and_14 (and_14_out, not_3_out, S_1, not_6_out);
  and and_15 (and_15_out, not_4_out, S_1, S_0);
  and and_16 (and_16_out, S_5, S_2, not_6_out);
  and and_17 (and_17_out, not_1_out, not_2_out, not_3_out, S_0);
  and and_18 (and_18_out, S_3, S_2, not_6_out);
  and and_19 (and_19_out, S_4, S_2, not_6_out);
  and and_20 (and_20_out, S_2, not_5_out, S_0);
  and and_21 (and_21_out, not_1_out, not_2_out, not_5_out, S_0);
  or or_2 (C_2, and_4_out, and_5_out, and_6_out, and_7_out, and_8_out);
  or or_3 (C_1, and_9_out, and_10_out, and_11_out, and_12_out, and_13_out, and_14_out);
  or or_4 (C_0, and_15_out, and_16_out, and_17_out, and_18_out, and_19_out, and_20_out, and_21_out);
endmodule

module State_to_Lights (
  input  S_5,
  input  S_4,
  input  S_3,
  input  S_2,
  input  S_1,
  input  S_0,
  output LE_R,
  output LE_Y,
  output LE_G,
  output LX_R,
  output LX_Y,
  output LX_G
);

  wire and_1_out, and_2_out, and_3_out, and_4_out, and_5_out, and_6_out, and_7_out, and_8_out, and_9_out,
       and_10_out, and_11_out, and_12_out, and_13_out, and_14_out, and_15_out, and_16_out, and_17_out,
       and_18_out, and_19_out, and_20_out, and_21_out, and_22_out, and_23_out, and_24_out, and_25_out,
       not_1_out, not_2_out, not_3_out, not_4_out, not_5_out, not_6_out;

  not not_1 (not_1_out, S_5);
  not not_2 (not_2_out, S_4);
  not not_3 (not_3_out, S_3);
  not not_4 (not_4_out, S_2);
  not not_5 (not_5_out, S_1);
  not not_6 (not_6_out, S_0);
  and and_1 (and_1_out, S_5, not_5_out);
  and and_2 (and_2_out, not_1_out, not_2_out, S_3, not_4_out, S_1, not_6_out);
  and and_3 (and_3_out, S_3, S_2, not_5_out);
  and and_4 (and_4_out, S_4, not_5_out);
  and and_5 (and_5_out, S_4, S_1, S_0);
  and and_6 (and_6_out, S_5, S_1, S_0);
  or or_1 (LE_Y, and_5_out, and_6_out, and_7_out);
  and and_7 (and_7_out, S_3, S_1, S_0);
  and and_8 (and_8_out, not_1_out, not_2_out, not_3_out);
  and and_9 (and_9_out, not_1_out, not_2_out, not_4_out, not_5_out);
  and and_10 (and_10_out, S_5, S_1, not_6_out);
  and and_11 (and_11_out, S_2, S_1, not_6_out);
  and and_12 (and_12_out, S_4, S_1, not_6_out);
  and and_13 (and_13_out, not_1_out, not_2_out, not_3_out);
  and and_14 (and_14_out, not_1_out, not_2_out, not_4_out, not_5_out);
  and and_15 (and_15_out, S_2, S_1);
  and and_16 (and_16_out, S_4, S_1);
  and and_17 (and_17_out, S_5, S_1);
  and and_18 (and_18_out, S_1, S_0);
  and and_19 (and_19_out, S_4, not_5_out, S_0);
  and and_20 (and_20_out, S_5, not_5_out, S_0);
  and and_21 (and_21_out, not_1_out, not_2_out, S_3, not_4_out, S_1, not_6_out);
  and and_22 (and_22_out, S_3, S_2, not_5_out, S_0);
  and and_23 (and_23_out, S_4, not_5_out, not_6_out);
  and and_24 (and_24_out, S_5, not_5_out, not_6_out);
  or or_2 (LX_G, and_23_out, and_24_out, and_25_out);
  and and_25 (and_25_out, S_3, S_2, not_5_out, not_6_out);
  or or_3 (LE_R, and_1_out, and_2_out, and_3_out, and_4_out);
  or or_4 (LE_G, and_8_out, and_9_out, and_10_out, and_11_out, and_12_out);
  or or_5 (LX_R, and_13_out, and_14_out, and_15_out, and_16_out, and_17_out, and_18_out);
  or or_6 (LX_Y, and_19_out, and_20_out, and_21_out, and_22_out);
endmodule

module State_Transition (
  input  S_5,
  input  S_4,
  input  S_3,
  input  S_2,
  input  S_1,
  input  S_0,
  input  Enter,
  input  Exit,
  output O_5,
  output O_4,
  output O_3,
  output O_2,
  output O_1,
  output O_0
);

  wire and_1_out, and_2_out, and_3_out, and_4_out, and_5_out, and_6_out, and_7_out, and_8_out, and_9_out,
       and_10_out, and_11_out, and_12_out, and_13_out, and_14_out, and_15_out, and_16_out, and_17_out,
       and_18_out, and_19_out, and_20_out, and_21_out, and_22_out, and_23_out, and_24_out, and_25_out,
       and_26_out, and_27_out, and_28_out, and_29_out, and_30_out, and_31_out, and_32_out, and_33_out,
       and_34_out, and_35_out, and_36_out, and_37_out, and_38_out, and_39_out, and_40_out, and_41_out,
       and_42_out, and_43_out, and_44_out, and_45_out, and_46_out, and_47_out, and_48_out, and_49_out,
       and_50_out, and_51_out, and_52_out, and_53_out, and_54_out, and_55_out, and_56_out, and_57_out,
       and_58_out, and_59_out, and_60_out, and_61_out, and_62_out, and_63_out, and_64_out, and_65_out,
       and_66_out, and_67_out, and_68_out, and_69_out, and_70_out, and_71_out, and_72_out, not_1_out,
       not_2_out, not_3_out, not_4_out, not_5_out, not_6_out, not_7_out, not_8_out;

  not not_1 (not_1_out, S_5);
  not not_2 (not_2_out, S_4);
  not not_3 (not_3_out, S_3);
  not not_4 (not_4_out, S_2);
  not not_5 (not_5_out, S_1);
  not not_6 (not_6_out, S_0);
  not not_7 (not_7_out, Enter);
  not not_8 (not_8_out, Exit);
  and and_1 (and_1_out, S_5, not_5_out, not_8_out);
  and and_2 (and_2_out, S_5, S_0);
  and and_3 (and_3_out, S_5, S_2, not_5_out);
  and and_4 (and_4_out, not_2_out, not_3_out, S_2, S_1, S_0, Exit);
  and and_5 (and_5_out, not_2_out, S_3, not_4_out, not_5_out, Exit);
  and and_6 (and_6_out, not_2_out, S_3, not_4_out, not_5_out, S_0);
  and and_7 (and_7_out, S_4, S_3, S_2, S_1, S_0);
  and and_8 (and_8_out, S_5, not_3_out, not_4_out, not_5_out, not_6_out, Exit);
  and and_9 (and_9_out, not_1_out, not_3_out, not_4_out, S_1, S_0, Exit);
  and and_10 (and_10_out, not_1_out, not_3_out, S_2, not_5_out, Exit);
  and and_11 (and_11_out, not_1_out, not_2_out, not_3_out, S_2, not_6_out, Exit);
  and and_12 (and_12_out, not_2_out, S_3, S_2, S_1, S_0);
  and and_13 (and_13_out, S_4, not_5_out, not_8_out);
  and and_14 (and_14_out, S_4, not_3_out, S_0);
  and and_15 (and_15_out, S_4, S_3, not_5_out);
  and and_16 (and_16_out, S_4, not_4_out, S_0);
  and and_17 (and_17_out, S_5, not_3_out, not_4_out, not_5_out, not_6_out, Exit);
  and and_18 (and_18_out, not_1_out, not_2_out, not_5_out, S_0, Exit);
  and and_19 (and_19_out, not_1_out, not_2_out, not_3_out, S_1, not_6_out, Exit);
  and and_20 (and_20_out, S_5, S_2, S_1, Enter);
  and and_21 (and_21_out, S_5, S_2, S_1, S_0);
  and and_22 (and_22_out, not_3_out, S_2, S_1, S_0, Enter, not_8_out);
  and and_23 (and_23_out, S_3, not_5_out, not_8_out);
  and and_24 (and_24_out, S_5, S_3, S_1);
  and and_25 (and_25_out, S_3, not_4_out, S_0);
  and and_26 (and_26_out, S_3, S_2, not_5_out);
  and and_27 (and_27_out, S_4, not_3_out, not_4_out, not_5_out, not_6_out, Exit);
  and and_28 (and_28_out, S_4, not_3_out, S_2, S_1, S_0);
  and and_29 (and_29_out, S_5, not_3_out, not_4_out, S_1);
  and and_30 (and_30_out, not_4_out, S_1, S_0, Enter, not_8_out);
  and and_31 (and_31_out, not_1_out, not_2_out, not_3_out, S_2, not_6_out);
  and and_32 (and_32_out, S_2, not_5_out, not_8_out);
  and and_33 (and_33_out, S_5, S_2, not_5_out, S_0);
  and and_34 (and_34_out, not_1_out, not_2_out, not_3_out, S_2, not_7_out, not_8_out);
  and and_35 (and_35_out, S_3, not_4_out, not_5_out, not_6_out, Exit);
  and and_36 (and_36_out, S_3, not_4_out, S_1, S_0);
  and and_37 (and_37_out, S_3, S_2, not_5_out, S_0);
  and and_38 (and_38_out, S_4, not_4_out, not_5_out, not_6_out, Exit);
  and and_39 (and_39_out, S_4, not_4_out, S_1, S_0);
  and and_40 (and_40_out, S_4, S_2, not_5_out, S_0);
  and and_41 (and_41_out, S_4, S_3, S_1, not_6_out);
  and and_42 (and_42_out, S_5, not_4_out, not_5_out, not_6_out, Exit);
  and and_43 (and_43_out, S_5, not_3_out, S_1, not_6_out, not_7_out);
  and and_44 (and_44_out, not_1_out, not_2_out, not_3_out, S_1, not_6_out, Exit);
  and and_45 (and_45_out, S_4, S_2, S_1, not_6_out, Enter);
  and and_46 (and_46_out, S_5, not_5_out, S_0);
  and and_47 (and_47_out, not_5_out, S_0, Enter);
  and and_48 (and_48_out, not_3_out, not_4_out, S_1, not_6_out);
  and and_49 (and_49_out, not_1_out, not_2_out, not_3_out, S_1, not_7_out);
  and and_50 (and_50_out, not_1_out, not_2_out, S_3, not_5_out, Exit);
  and and_51 (and_51_out, S_3, not_5_out, S_0);
  and and_52 (and_52_out, S_4, not_5_out, S_0);
  and and_53 (and_53_out, not_3_out, S_1, not_6_out, not_7_out);
  and and_54 (and_54_out, S_3, S_2, S_1, not_6_out, Enter);
  and and_55 (and_55_out, not_1_out, not_2_out, not_3_out, S_0, Exit);
  and and_56 (and_56_out, not_1_out, not_2_out, not_3_out, S_2, Exit);
  and and_57 (and_57_out, not_1_out, not_2_out, not_3_out, S_1, not_6_out);
  and and_58 (and_58_out, not_1_out, not_2_out, not_3_out, S_1, Exit);
  and and_59 (and_59_out, not_1_out, not_2_out, not_3_out, S_0, not_7_out);
  and and_60 (and_60_out, not_1_out, not_2_out, not_3_out, S_2, Exit);
  and and_61 (and_61_out, not_3_out, not_5_out, not_6_out, Enter, not_8_out);
  and and_62 (and_62_out, S_5, S_2, S_1, not_6_out, not_7_out);
  and and_63 (and_63_out, not_1_out, not_2_out, not_3_out, not_6_out, Enter);
  and and_64 (and_64_out, not_1_out, not_2_out, S_3, not_4_out, not_5_out, Exit);
  and and_65 (and_65_out, not_1_out, not_5_out, not_6_out, Enter, not_8_out);
  and and_66 (and_66_out, S_3, S_2, S_1, not_6_out, not_7_out);
  and and_67 (and_67_out, S_4, S_2, S_1, not_6_out, not_7_out);
  and and_68 (and_68_out, S_4, not_4_out, S_1, not_6_out, Enter);
  and and_69 (and_69_out, S_5, not_4_out, S_1, not_6_out, Enter);
  and and_70 (and_70_out, S_5, not_4_out, not_6_out, Enter, not_8_out);
  and and_71 (and_71_out, not_1_out, not_2_out, S_3, not_4_out, not_5_out, S_0);
  and and_72 (and_72_out, not_1_out, not_2_out, not_3_out, Enter, Exit);
  or or_1 (O_5, and_1_out, and_2_out, and_3_out, and_4_out, and_5_out, and_6_out, and_7_out);
  or or_2 (O_4, and_8_out, and_9_out, and_10_out, and_11_out, and_12_out, and_13_out, and_14_out, and_15_out, and_16_out);
  or or_3 (O_3, and_17_out, and_18_out, and_19_out, and_20_out, and_21_out, and_22_out, and_23_out, and_24_out, and_25_out, and_26_out, and_27_out, and_28_out);
  or or_4 (O_2, and_29_out, and_30_out, and_31_out, and_32_out, and_33_out, and_34_out, and_35_out, and_36_out, and_37_out, and_38_out, and_39_out, and_40_out, and_41_out, and_42_out, and_43_out, and_44_out, and_45_out);
  or or_5 (O_1, and_46_out, and_47_out, and_48_out, and_49_out, and_50_out, and_51_out, and_52_out, and_53_out, and_54_out, and_55_out, and_56_out, and_57_out);
  or or_6 (O_0, and_58_out, and_59_out, and_60_out, and_61_out, and_62_out, and_63_out, and_64_out, and_65_out, and_66_out, and_67_out, and_68_out, and_69_out, and_70_out, and_71_out, and_72_out);
endmodule
